# Fritzing sketch RJ45-twister (saved by Fritzing 0.9.5d)
circuit board: 10.6836cm x 3.89786cm
breadboards: 1

parts:
  U1 = XPORT [package=xport]
  U2 = XPORT [package=xport]
  J5 = female pin header, 8 pins [form="♀ (female)"]
  J6 = double row female pin header, 16 pins [form="♀ (female)"]
  J4 = female pin header, 8 pins [form="♀ (female)"]

nets:
  N1: U1.GND, J6.pin16, J4.pin1
  N2: U1.3.3V, J6.pin15, J4.pin2
  N3: U1.RST, J6.pin14, J4.pin3
  N4: U1.TX, J6.pin13, J4.pin4
  N5: U1.RX, J6.pin12, J4.pin5
  N6: U1.RTS, J6.pin11, J4.pin6
  N7: U1.DTR, J6.pin10, J4.pin7
  N8: U1.CTS, J6.pin9, J4.pin8
  N9: U2.GND, J5.pin1, J6.pin1
  N10: U2.3.3V, J5.pin2, J6.pin2
  N11: U2.RST, J5.pin3, J6.pin3
  N12: U2.TX, J5.pin4, J6.pin4
  N13: U2.RX, J5.pin5, J6.pin5
  N14: U2.RTS, J5.pin6, J6.pin6
  N15: U2.DTR, J5.pin7, J6.pin7
  N16: U2.CTS, J5.pin8, J6.pin8
